# Fritzing sketch circuit_layout (saved by Fritzing 0.9.3b)
perfboards: 1

parts:
  U1 = NodeMCU V1.0  # not connected
  IC1 = SELECTOR_MULTIPLEXER [package=dil16]
  JP2 = Header 1 [package=1x01_offset]  # not connected
  JP3 = Header 1 [package=1x01_offset]  # not connected
  JP4 = Header 1 [package=1x01_offset]  # not connected
  R2 = Resistor [tolerance=±1% resistance=15k package=THT]
  JP5 = Header 1 [package=1x01_offset]  # not connected
  JP6 = Header 1 [package=1x01_offset]  # not connected
  JP7 = Header 1 [package=1x01_offset]  # not connected
  JP8 = Header 1 [package=1x01_offset]
  JP9 = Header 1 [package=1x01_offset]  # not connected
  JP10 = Header 1 [package=1x01_offset]  # not connected
  JP11 = Header 1 [package=1x01_offset]  # not connected
  JP13 = Header 1 [package=1x01_offset]  # not connected
  R3 = Resistor [tolerance=±1% resistance=15k package=THT]  # not connected
  Q1 = TRANSISTOR_PNP [package=to-92]  # not connected
  R4 = Resistor [tolerance=±1% resistance=2.2k package=THT]  # not connected
  JP15 = Header 1 [package=1x01_offset]  # not connected
  JP16 = Header 1 [package=1x01_offset]
  JP17 = Header 1 [package=1x01_offset]  # not connected
  JP18 = Header 1 [package=1x01_offset]  # not connected
  JP19 = Header 1 [package=1x01_offset]  # not connected
  JP20 = Header 1 [package=1x01_offset]  # not connected
  JP21 = Header 1 [package=1x01_offset]
  JP22 = Header 1 [package=1x01_offset]
  JP23 = Header 1 [package=1x01_offset]  # not connected
  JP24 = Header 1 [package=1x01_offset]  # not connected
  JP25 = Header 1 [package=1x01_offset]  # not connected
  JP27 = Header 1 [package=1x01_offset]  # not connected
  JP28 = Header 1 [package=1x01_offset]  # not connected
  JP29 = Header 1 [package=1x01_offset]  # not connected
  JP30 = Header 1 [package=1x01_offset]  # not connected
  J4 = Power Jack [package=power_jack_smd]  # not connected
  JP31 = Header 1 [package=1x01_offset]  # not connected
  JP32 = Header 1 [package=1x01_offset]
  JP33 = Header 1 [package=1x01_offset]  # not connected
  JP34 = Header 1 [package=1x01_offset]  # not connected
  JP35 = Header 1 [package=1x01_offset]  # not connected
  Q3 = NPN-Transistor [package="TO92 [THT]"]  # not connected
  R6 = Resistor [tolerance=±1% resistance=10k package=THT]  # not connected
  JP36 = Header 1 [package=1x01_offset]  # not connected
  JP38 = Header 1 [package=1x01_offset]
  J5 = Basic Servo
  Bauteil1 = Soil Moisture Sensor
  M1 = DC Motor
  JP39 = Header 1 [package=1x01_offset]  # not connected
  LM1 = RioRand LM2596  # not connected

nets:
  N1: IC1.Analog_Port, R2.Pin_0
  N2: IC1.INH, IC1.VEE, IC1.GND
  N3: JP8.1, Bauteil1.SIG
  N4: JP16.1, J5.pulse
  N5: JP21.1, Bauteil1.GND
  N6: JP22.1, Bauteil1.VCC
  N7: JP32.1, M1.pin_2
  N8: JP38.1, M1.pin_1

notes:
  Pump
  12V
  12V to 5V

custom parts:
  NodeMCU V1.0: ESP8266 based NodeMCU
  SELECTOR_MULTIPLEXER: Quadruple 2-line to 1-line data SELECTOR/MULTIPLEXER
  NPN-Transistor: A standard NPN-transistor
